# Fritzing sketch wiring diagram (saved by Fritzing 1.0.2b)

parts:
  Part1 = Adafruit KB2040
  Part2 = Adafruit DRV8833 DC/Stepper Motor Driver [part_number="Adafruit #3297"]
  M1 = DC Motor [voltage_(max)=6V voltage_(min)=3V]
  U1 = LIPO-1000mAh [package=lipo-1000]
  U2 = LIPO-110mAh [package=lipo-110]

nets:
  GND: Part1.GND, Part2.GND, U1.-, U2.-
  N1: Part1.RAW, U2.+
  N2: Part1.D2, Part2.AIN1
  N3: Part1.D3, Part2.AIN2
  N4: Part1.D6, Part2.!SLEEP
  N5: Part2.PWRIN, U1.+
  N6: Part2.AOUT2, M1.pin_1
  N7: Part2.AOUT1, M1.pin_2

custom parts:
  Adafruit DRV8833 DC/Stepper Motor Driver: Spin two DC motors or step one bi-polar or uni-polar stepper with up to 1.2A per channel using the DRV8833. This motor driver chip is a nice alternative to the TB6612 driver. Like that chip, you get 2 full H-bridges, but this chip is better for low voltage uses (can run from 2.7V up to 10.8V motor power) and has built in current limiting capability. We set it up for 1A current limiting so you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
