# Fritzing sketch wiring_diagram (saved by Fritzing 1.0.2b)

parts:
  Part1 = Adafruit KB2040
  Part2 = Adafruit DRV8833 DC/Stepper Motor Driver [part_number="Adafruit #3297"]
  Motor_A = DC Motor [voltage_(max)=6V voltage_(min)=3V]
  Part3 = US-100 Ultrasonic Rangefinder
  Adafruit_USB_Type_C_Plug_Breakout1 = Adafruit USB Type C Plug Breakout [part_number=#5978]
  Motor_B = DC Motor [voltage_(max)=6V voltage_(min)=3V]
  R1 = Resistor [tolerance=±5% power=0.25W resistance=10k package=THT]
  R2 = Resistor [tolerance=±5% power=0.25W resistance=10k package=THT]
  BAT1 = Battery Holders [package=battery-aa]
  BAT2 = Battery Holders [package=battery-aa]
  BAT3 = Battery Holders [package=battery-aa]
  BAT4 = Battery Holders [package=battery-aa]
  U1 = Battery Holders [package=lipo-1100mAh]

nets:
  GND: Part1.GND, Part2.GND, Part3.GND, R2.Pin_1, BAT4.-
  N1: Part1.A2, R1.Pin_0, R2.Pin_0
  N2: Part1.A3, Part3.Trig/Tx
  N3: Part1.RAW, Part3.VCC
  N4: Part1.D2, Part2.AIN1
  N5: Part1.D3, Part2.AIN2
  N6: Part1.D4, Part2.BIN1
  N7: Part1.D5, Part2.BIN2
  N8: Part1.D6, Part2.!SLEEP
  N9: Part2.PWRIN, BAT1.+
  N10: Part2.AOUT2, Motor_A.pin_1
  N11: Part2.AOUT1, Motor_A.pin_2
  N12: Part2.BOUT1, Motor_B.pin_1
  N13: Part2.BOUT2, Motor_B.pin_2
  N14: Part3.Echo/Rx, R1.Pin_1
  N15: Adafruit_USB_Type_C_Plug_Breakout1.GND, U1.-
  N16: Adafruit_USB_Type_C_Plug_Breakout1.VBUS, U1.+
  N17: BAT1.-, BAT2.+
  N18: BAT2.-, BAT3.+
  N19: BAT3.-, BAT4.+

custom parts:
  Adafruit DRV8833 DC/Stepper Motor Driver: Spin two DC motors or step one bi-polar or uni-polar stepper with up to 1.2A per channel using the DRV8833. This motor driver chip is a nice alternative to the TB6612 driver. Like that chip, you get 2 full H-bridges, but this chip is better for low voltage uses (can run from 2.7V up to 10.8V motor power) and has built in current limiting capability. We set it up for 1A current limiting so you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
  Adafruit USB Type C Plug Breakout: Throw out all those Mini and Micro B USB cables you have in a plastic bin - the next generation of USB connectors is here with USB C! You've seen these connectors pop up on all sorts of devices, as the industry moves from micro B or lightning to the new standard. Well, at least until the next standard comes out USB C features a symmetric/reversible connector, more data pins and higher current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
